# Fritzing sketch lamp (saved by Fritzing 0.9.2b)
circuit board: 8.46667cm x 5.64444cm
breadboards: 1

parts:
  J5 = Power Jack [package=power_jack_combo]
  Part1 = Arduino Uno (Rev3)
  U4 = ESP8266 WiFi Module [part_number=ESP8266]
  U5 = Voltage Regulator - 3.3V [package="TO220 [THT]"]
  RGB_SMD_LED1 = SMD RGB LED (WS2812) [package=5050]

nets:
  GND: J5.GND, Part1.GND, U4.GND, U5.GND, RGB_SMD_LED1.VSS
  VIN: J5.PWR, Part1.VIN, U5.input_voltage, RGB_SMD_LED1.VDD
  N1: Part1.D11_PWM/MOSI, RGB_SMD_LED1.DIn
  N2: Part1.D2, U4.TXD
  N3: Part1.D3_PWM, U4.RXD
  N4: U4.VCC, U4.CH_PD, U5.output_voltage

custom parts:
  ESP8266 WiFi Module: Generic WiFi Module based on the ESP8266 with onboard PCB antenna and UART communications

// code stored in the sketch: lamp.ino
#include "FastLED.h"
#include "esp8266server.h"
#include "Lamp.h"
#include "animations.h"
//here we have included the animations we want to be able to use

#define LED_DATA_PIN 8
#define NUM_LEDS 50
//#define BRIGHTNESS  64
#define LED_TYPE WS2811
#define COLOR_ORDER RGB

#define MatrixWidth 4
#define MatrixHeight 10

//const uint8_t BUTTON_PIN = 2; //purple wire

volatile boolean next_animation = false;
volatile boolean on_off = true;

int animation = 0;

CRGB leds[NUM_LEDS];

Lamp* lamp;

iLampAnimation* ta;

void switchAnitmation() {
  if(on_off) {
    next_animation = true;
  }
}

void onOffToggle() {
  //this signifies that the off() function is to take over or end (toggle)
  on_off = !on_off;
  if(on_off) {
    lamp->turnOn();
  }
  else if(on_off == 0) {
    lamp->turnOff();
  }
}


void setup() {
  //Serial.begin(9600);
  Serial.begin(115200);
  FastLED.addLeds<LED_TYPE, LED_DATA_PIN, COLOR_ORDER>(leds, NUM_LEDS).setCorrection( TypicalLEDStrip );
  lamp = new Lamp(leds, NUM_LEDS, MatrixWidth);
  //go to white animation
  //setAnimation(99);
  //setup our server
  //esp8266ServerSetup(lamp);

  setAnimation(255);
}



void loop() {
  // if(next_animation) {
  //   next_animation = false;
  //   animation++;
  //   setAnimation(animation);
  // }
  //Serial.println(animation);
  int animation_delay = ta->itterate();
  int delayed = 0;
  while(delayed <= animation_delay) {
    process_request(&urlRouter);
    delay(1);
    delayed++;
  }
}

void white() {
  lamp->fill_color(0, NUM_LEDS-1, CRGB::White);
  lamp->render();
}

void black() {
  lamp->fill_color(0, NUM_LEDS-1, CRGB::Black);
  lamp->render();
}

void setAnimation(uint8_t whichanimation) {
  Serial.print("Setting animation to: ");
  Serial.println(whichanimation);
  switch(whichanimation) {
    case 0:
      ta = new RainbowFill(lamp);
      break;
    case 1:
      ta = new Fire(lamp);
      break;
    case 2:
      ta = new BarberPole(lamp);
      break;
    // case 3:
    //   ta = new DebugV(lamp);
    //   break;
    case 98:
      //default case re-sets the animation to first, re-runs
      ta = new iLampAnimation(lamp);
      black();
      break;
    case 99:
      //default case re-sets the animation to first, re-runs
      ta = new iLampAnimation(lamp);
      white();
      break;
    case 253:
      ta = new PancakeSort(lamp);
      break;
    case 254:
      ta = new Gradient1(lamp);
      break;
    case 255:
      ta = new Gradient2(lamp);
      break;
    default:
      setAnimation(99);
      break;
  }
  animation = whichanimation;
  next_animation = false;
}

String urlRouter(String url) {
  Serial.println(url);
  String resp = "";
  int anim_at = url.indexOf("/anim/");
  if(anim_at > -1) {
    int anim = url.substring(anim_at+6).toInt();
    setAnimation(anim);
  }
  int color_at = url.indexOf("/color/");
  if(color_at > -1) {
    setAnimation(99);
    //red for now
    lamp->fill_color(0, lamp->getNumLeds()-1, CRGB::Red);
    lamp->render();
  }
  resp+=animation;
  return resp;
}
