# Fritzing sketch lamp2 (saved by Fritzing 0.9.0b)
perfboards: 1

parts:
  Part1 = Arduino Uno (Rev3)
  J1 = Power Jack [package=power_jack_pth_lock]
  R2 = Resistor [package="2010 [SMD]"]
  S1 = Pushbutton [package="[THT]"]
  JP1 = Header 3 [package=screwterminal-3.5mm-3_lock.007s]
  R3 = Resistor [package="2010 [SMD]"]
  R4 = Resistor [package="2010 [SMD]"]
  R5 = Resistor [package="2010 [SMD]"]
  R6 = Resistor [package="2010 [SMD]"]
  R7 = Resistor [package="2010 [SMD]"]
  R8 = Resistor [package="2010 [SMD]"]
  U2 = Voltage Regulator - Variable [package="TO220 [THT]"]
  R9 = Resistor [package="2010 [SMD]"]
  R10 = Resistor [package="2010 [SMD]"]

nets:
  N1: Part1.D8, JP1.1
  GND: Part1.GND, J1.GND, R2.Pin_0, JP1.3
  N2: Part1.VIN, J1.PWR, JP1.2, U2.IN
  N3: R2.Pin_1, R3.Pin_1
  N4: S1.Pin_1, S1.Pin_2
  N5: S1.Pin_3, S1.Pin_4
  N6: R3.Pin_0, R4.Pin_0
  N7: R4.Pin_1, R5.Pin_0
  N8: R5.Pin_1, R6.Pin_0
  N9: R6.Pin_1, R7.Pin_1
  N10: R7.Pin_0, R8.Pin_0, U2.ADJ
  N11: R8.Pin_1, R10.Pin_0
  N12: U2.OUT, R9.Pin_0
  N13: R9.Pin_1, R10.Pin_1
